// Logisim project gal.circ as structural Verilog: 1 circuit, main circuit main
module main (
  input  in_1,
  input  in_2,
  input  in_3,
  input  in_4,
  input  in_5,
  input  in_6,
  input  in_7,
  input  in_8,
  input  in_9,
  input  in_10,
  input  in_11,
  input  in_12,
  input  in_13,
  input  in_14,
  input  in_15,
  input  in_16,
  input  in_17,
  input  in_18,
  input  in_19,
  input  in_20,
  input  in_21,
  input  in_22,
  input  A,
  input  \Ã ,
  input  B,
  input  nB,
  input  in_27,
  input  in_28,
  input  in_29,
  input  in_30,
  input  in_31,
  input  in_32,
  input  in_33,
  input  in_34,
  input  in_35,
  input  in_36,
  input  in_37,
  input  in_38,
  input  in_39,
  input  in_40,
  input  in_41,
  input  in_42,
  input  in_43,
  input  in_44,
  input  in_45,
  input  in_46,
  input  in_47,
  input  in_48,
  input  in_49,
  input  in_50,
  input  in_51,
  input  in_52,
  input  in_53,
  input  in_54,
  input  in_55,
  input  in_56,
  input  in_57,
  input  in_58,
  input  in_59,
  input  in_60,
  input  in_61,
  input  in_62,
  input  in_63,
  input  in_64,
  input  in_65,
  input  in_66,
  input  in_67,
  input  in_68,
  input  in_69,
  input  in_70,
  input  in_71,
  input  in_72,
  input  in_73,
  input  in_74,
  input  in_75,
  input  in_76,
  input  in_77,
  input  in_78,
  input  in_79,
  input  in_80,
  input  in_81,
  input  in_82,
  input  in_83,
  input  in_84,
  input  in_85,
  input  in_86,
  input  in_87,
  input  in_88,
  input  in_89,
  input  in_90,
  input  in_91,
  input  in_92,
  input  in_93,
  input  in_94,
  input  in_95,
  input  A_2,
  input  \Ã_2 ,
  input  B_2,
  input  nB_2,
  input  C,
  input  nC,
  output out_102,
  output out_103
);

  wire and_1_out, and_2_out, and_3_out, and_4_out, and_5_out, and_6_out, and_7_out, controlled_buffer_1_out,
       controlled_buffer_3_out, controlled_buffer_5_out, controlled_buffer_7_out, controlled_buffer_9_out,
       controlled_buffer_11_out, controlled_buffer_13_out, controlled_buffer_15_out,
       controlled_buffer_17_out, controlled_buffer_19_out, controlled_buffer_21_out,
       controlled_buffer_23_out, controlled_buffer_25_out, controlled_buffer_27_out,
       controlled_buffer_29_out, controlled_buffer_31_out, controlled_buffer_33_out,
       controlled_buffer_35_out, controlled_buffer_76_out, controlled_buffer_79_out, not_1_out, not_2_out,
       not_3_out, not_4_out, not_5_out;

  not not_1 (not_1_out, in_1);
  assign controlled_buffer_1_out = in_4 ? not_1_out : 1'bz;  // Controlled_Buffer controlled_buffer_1
  assign controlled_buffer_1_out = in_3 ? in_1 : 1'bz;  // Controlled_Buffer controlled_buffer_2
  assign controlled_buffer_3_out = in_8 ? not_1_out : 1'bz;  // Controlled_Buffer controlled_buffer_3
  assign controlled_buffer_3_out = in_7 ? in_1 : 1'bz;  // Controlled_Buffer controlled_buffer_4
  assign controlled_buffer_5_out = in_12 ? not_1_out : 1'bz;  // Controlled_Buffer controlled_buffer_5
  assign controlled_buffer_5_out = in_11 ? in_1 : 1'bz;  // Controlled_Buffer controlled_buffer_6
  assign controlled_buffer_7_out = in_15 ? in_1 : 1'bz;  // Controlled_Buffer controlled_buffer_7
  assign controlled_buffer_7_out = in_16 ? not_1_out : 1'bz;  // Controlled_Buffer controlled_buffer_8
  assign controlled_buffer_9_out = in_19 ? in_1 : 1'bz;  // Controlled_Buffer controlled_buffer_9
  assign controlled_buffer_9_out = in_20 ? not_1_out : 1'bz;  // Controlled_Buffer controlled_buffer_10
  assign controlled_buffer_11_out = A ? in_1 : 1'bz;  // Controlled_Buffer controlled_buffer_11
  assign controlled_buffer_11_out = \Ã  ? not_1_out : 1'bz;  // Controlled_Buffer controlled_buffer_12
  not not_2 (not_2_out, in_27);
  assign controlled_buffer_13_out = in_31 ? not_2_out : 1'bz;  // Controlled_Buffer controlled_buffer_13
  assign controlled_buffer_13_out = in_30 ? in_27 : 1'bz;  // Controlled_Buffer controlled_buffer_14
  assign controlled_buffer_15_out = in_36 ? in_27 : 1'bz;  // Controlled_Buffer controlled_buffer_15
  assign controlled_buffer_15_out = in_37 ? not_2_out : 1'bz;  // Controlled_Buffer controlled_buffer_16
  assign controlled_buffer_17_out = in_43 ? not_2_out : 1'bz;  // Controlled_Buffer controlled_buffer_17
  assign controlled_buffer_17_out = in_42 ? in_27 : 1'bz;  // Controlled_Buffer controlled_buffer_18
  assign controlled_buffer_19_out = in_48 ? in_27 : 1'bz;  // Controlled_Buffer controlled_buffer_19
  assign controlled_buffer_19_out = in_49 ? not_2_out : 1'bz;  // Controlled_Buffer controlled_buffer_20
  assign controlled_buffer_21_out = in_54 ? in_27 : 1'bz;  // Controlled_Buffer controlled_buffer_21
  assign controlled_buffer_21_out = in_55 ? not_2_out : 1'bz;  // Controlled_Buffer controlled_buffer_22
  assign controlled_buffer_23_out = in_60 ? in_27 : 1'bz;  // Controlled_Buffer controlled_buffer_23
  assign controlled_buffer_23_out = in_61 ? not_2_out : 1'bz;  // Controlled_Buffer controlled_buffer_24
  assign controlled_buffer_25_out = in_67 ? not_2_out : 1'bz;  // Controlled_Buffer controlled_buffer_25
  assign controlled_buffer_25_out = in_66 ? in_27 : 1'bz;  // Controlled_Buffer controlled_buffer_26
  assign controlled_buffer_27_out = in_72 ? in_27 : 1'bz;  // Controlled_Buffer controlled_buffer_27
  assign controlled_buffer_27_out = in_73 ? not_2_out : 1'bz;  // Controlled_Buffer controlled_buffer_28
  assign controlled_buffer_29_out = in_78 ? in_27 : 1'bz;  // Controlled_Buffer controlled_buffer_29
  assign controlled_buffer_29_out = in_79 ? not_2_out : 1'bz;  // Controlled_Buffer controlled_buffer_30
  assign controlled_buffer_31_out = in_84 ? in_27 : 1'bz;  // Controlled_Buffer controlled_buffer_31
  assign controlled_buffer_31_out = in_85 ? not_2_out : 1'bz;  // Controlled_Buffer controlled_buffer_32
  assign controlled_buffer_33_out = in_91 ? not_2_out : 1'bz;  // Controlled_Buffer controlled_buffer_33
  assign controlled_buffer_33_out = in_90 ? in_27 : 1'bz;  // Controlled_Buffer controlled_buffer_34
  assign controlled_buffer_35_out = \Ã_2  ? not_2_out : 1'bz;  // Controlled_Buffer controlled_buffer_35
  assign controlled_buffer_35_out = A_2 ? in_27 : 1'bz;  // Controlled_Buffer controlled_buffer_36
  assign controlled_buffer_1_out = in_5 ? in_2 : 1'bz;  // Controlled_Buffer controlled_buffer_37
  assign controlled_buffer_3_out = in_9 ? in_2 : 1'bz;  // Controlled_Buffer controlled_buffer_38
  assign controlled_buffer_5_out = in_13 ? in_2 : 1'bz;  // Controlled_Buffer controlled_buffer_39
  assign controlled_buffer_7_out = in_17 ? in_2 : 1'bz;  // Controlled_Buffer controlled_buffer_40
  assign controlled_buffer_9_out = in_21 ? in_2 : 1'bz;  // Controlled_Buffer controlled_buffer_41
  assign controlled_buffer_11_out = B ? in_2 : 1'bz;  // Controlled_Buffer controlled_buffer_42
  assign controlled_buffer_13_out = in_32 ? in_28 : 1'bz;  // Controlled_Buffer controlled_buffer_43
  assign controlled_buffer_15_out = in_38 ? in_28 : 1'bz;  // Controlled_Buffer controlled_buffer_44
  assign controlled_buffer_17_out = in_44 ? in_28 : 1'bz;  // Controlled_Buffer controlled_buffer_45
  assign controlled_buffer_19_out = in_50 ? in_28 : 1'bz;  // Controlled_Buffer controlled_buffer_46
  assign controlled_buffer_21_out = in_56 ? in_28 : 1'bz;  // Controlled_Buffer controlled_buffer_47
  assign controlled_buffer_23_out = in_62 ? in_28 : 1'bz;  // Controlled_Buffer controlled_buffer_48
  assign controlled_buffer_25_out = in_68 ? in_28 : 1'bz;  // Controlled_Buffer controlled_buffer_49
  assign controlled_buffer_27_out = in_74 ? in_28 : 1'bz;  // Controlled_Buffer controlled_buffer_50
  assign controlled_buffer_29_out = in_80 ? in_28 : 1'bz;  // Controlled_Buffer controlled_buffer_51
  assign controlled_buffer_31_out = in_86 ? in_28 : 1'bz;  // Controlled_Buffer controlled_buffer_52
  assign controlled_buffer_33_out = in_92 ? in_28 : 1'bz;  // Controlled_Buffer controlled_buffer_53
  assign controlled_buffer_35_out = B_2 ? in_28 : 1'bz;  // Controlled_Buffer controlled_buffer_54
  not not_3 (not_3_out, in_2);
  assign controlled_buffer_1_out = in_6 ? not_3_out : 1'bz;  // Controlled_Buffer controlled_buffer_55
  assign controlled_buffer_3_out = in_10 ? not_3_out : 1'bz;  // Controlled_Buffer controlled_buffer_56
  assign controlled_buffer_5_out = in_14 ? not_3_out : 1'bz;  // Controlled_Buffer controlled_buffer_57
  assign controlled_buffer_7_out = in_18 ? not_3_out : 1'bz;  // Controlled_Buffer controlled_buffer_58
  assign controlled_buffer_9_out = in_22 ? not_3_out : 1'bz;  // Controlled_Buffer controlled_buffer_59
  assign controlled_buffer_11_out = nB ? not_3_out : 1'bz;  // Controlled_Buffer controlled_buffer_60
  not not_4 (not_4_out, in_28);
  assign controlled_buffer_13_out = in_33 ? not_4_out : 1'bz;  // Controlled_Buffer controlled_buffer_61
  assign controlled_buffer_15_out = in_39 ? not_4_out : 1'bz;  // Controlled_Buffer controlled_buffer_62
  assign controlled_buffer_17_out = in_45 ? not_4_out : 1'bz;  // Controlled_Buffer controlled_buffer_63
  assign controlled_buffer_19_out = in_51 ? not_4_out : 1'bz;  // Controlled_Buffer controlled_buffer_64
  assign controlled_buffer_21_out = in_57 ? not_4_out : 1'bz;  // Controlled_Buffer controlled_buffer_65
  assign controlled_buffer_23_out = in_63 ? not_4_out : 1'bz;  // Controlled_Buffer controlled_buffer_66
  assign controlled_buffer_25_out = in_69 ? not_4_out : 1'bz;  // Controlled_Buffer controlled_buffer_67
  assign controlled_buffer_27_out = in_75 ? not_4_out : 1'bz;  // Controlled_Buffer controlled_buffer_68
  assign controlled_buffer_29_out = in_81 ? not_4_out : 1'bz;  // Controlled_Buffer controlled_buffer_69
  assign controlled_buffer_31_out = in_87 ? not_4_out : 1'bz;  // Controlled_Buffer controlled_buffer_70
  assign controlled_buffer_33_out = in_93 ? not_4_out : 1'bz;  // Controlled_Buffer controlled_buffer_71
  assign controlled_buffer_35_out = nB_2 ? not_4_out : 1'bz;  // Controlled_Buffer controlled_buffer_72
  assign controlled_buffer_13_out = in_34 ? in_29 : 1'bz;  // Controlled_Buffer controlled_buffer_73
  assign controlled_buffer_15_out = in_40 ? in_29 : 1'bz;  // Controlled_Buffer controlled_buffer_74
  assign controlled_buffer_17_out = in_46 ? in_29 : 1'bz;  // Controlled_Buffer controlled_buffer_75
  assign controlled_buffer_76_out = in_52 ? in_29 : 1'bz;  // Controlled_Buffer controlled_buffer_76
  assign controlled_buffer_21_out = in_58 ? in_29 : 1'bz;  // Controlled_Buffer controlled_buffer_77
  assign controlled_buffer_23_out = in_64 ? in_29 : 1'bz;  // Controlled_Buffer controlled_buffer_78
  assign controlled_buffer_79_out = in_70 ? in_29 : 1'bz;  // Controlled_Buffer controlled_buffer_79
  assign controlled_buffer_27_out = in_76 ? in_29 : 1'bz;  // Controlled_Buffer controlled_buffer_80
  assign controlled_buffer_29_out = in_82 ? in_29 : 1'bz;  // Controlled_Buffer controlled_buffer_81
  assign controlled_buffer_31_out = in_88 ? in_29 : 1'bz;  // Controlled_Buffer controlled_buffer_82
  assign controlled_buffer_33_out = in_94 ? in_29 : 1'bz;  // Controlled_Buffer controlled_buffer_83
  assign controlled_buffer_35_out = C ? in_29 : 1'bz;  // Controlled_Buffer controlled_buffer_84
  and and_1 (and_1_out, controlled_buffer_1_out, controlled_buffer_3_out);
  and and_2 (and_2_out, controlled_buffer_5_out, controlled_buffer_7_out);
  and and_3 (and_3_out, controlled_buffer_9_out, controlled_buffer_11_out);
  not not_5 (not_5_out, in_29);
  assign controlled_buffer_13_out = in_35 ? not_5_out : 1'bz;  // Controlled_Buffer controlled_buffer_85
  assign controlled_buffer_15_out = in_41 ? not_5_out : 1'bz;  // Controlled_Buffer controlled_buffer_86
  assign controlled_buffer_17_out = in_47 ? not_5_out : 1'bz;  // Controlled_Buffer controlled_buffer_87
  assign controlled_buffer_76_out = in_53 ? not_5_out : 1'bz;  // Controlled_Buffer controlled_buffer_88
  assign controlled_buffer_21_out = in_59 ? not_5_out : 1'bz;  // Controlled_Buffer controlled_buffer_89
  assign controlled_buffer_23_out = in_65 ? not_5_out : 1'bz;  // Controlled_Buffer controlled_buffer_90
  assign controlled_buffer_79_out = in_71 ? not_5_out : 1'bz;  // Controlled_Buffer controlled_buffer_91
  assign controlled_buffer_27_out = in_77 ? not_5_out : 1'bz;  // Controlled_Buffer controlled_buffer_92
  assign controlled_buffer_29_out = in_83 ? not_5_out : 1'bz;  // Controlled_Buffer controlled_buffer_93
  assign controlled_buffer_31_out = in_89 ? not_5_out : 1'bz;  // Controlled_Buffer controlled_buffer_94
  assign controlled_buffer_33_out = in_95 ? not_5_out : 1'bz;  // Controlled_Buffer controlled_buffer_95
  assign controlled_buffer_35_out = nC ? not_5_out : 1'bz;  // Controlled_Buffer controlled_buffer_96
  or or_1 (out_102, and_1_out, and_2_out, and_3_out);
  and and_4 (and_4_out, controlled_buffer_13_out, controlled_buffer_15_out, controlled_buffer_17_out);
  and and_5 (and_5_out, controlled_buffer_76_out, controlled_buffer_21_out, controlled_buffer_23_out);
  and and_6 (and_6_out, controlled_buffer_79_out, controlled_buffer_27_out, controlled_buffer_29_out);
  and and_7 (and_7_out, controlled_buffer_31_out, controlled_buffer_33_out, controlled_buffer_35_out);
  or or_2 (out_103, and_4_out, and_5_out, and_6_out, and_7_out);
endmodule
