// Logisim project pal-gal.circ as structural Verilog: 1 circuit, main circuit main
module main (
  input  in_1,
  input  in_2,
  input  in_3,
  input  in_4,
  input  in_5,
  input  in_6,
  input  in_7,
  input  in_8,
  input  in_9,
  input  in_10,
  input  in_11,
  input  in_12,
  input  in_13,
  input  in_14,
  input  in_15,
  input  in_16,
  input  in_17,
  input  in_18,
  input  in_19,
  input  in_20,
  input  in_21,
  input  in_22,
  input  in_23,
  input  in_24,
  input  in_25,
  input  in_26,
  input  in_27,
  input  in_28,
  input  in_29,
  input  in_30,
  input  in_31,
  input  in_32,
  input  in_33,
  input  in_34,
  input  in_35,
  input  in_36,
  input  in_37,
  input  in_38,
  input  in_39,
  input  in_40,
  input  in_41,
  input  in_42,
  input  in_43,
  input  in_44,
  input  in_45,
  input  in_46,
  input  in_47,
  input  in_48,
  input  in_49,
  input  in_50,
  input  in_51,
  input  in_52,
  input  in_53,
  input  in_54,
  input  in_55,
  input  in_56,
  input  in_57,
  input  in_58,
  input  in_59,
  input  in_60,
  input  in_61,
  input  in_62,
  input  in_63,
  input  in_64,
  input  in_65,
  input  in_66,
  input  in_67,
  input  in_68,
  input  in_69,
  input  \Ã ,
  input  in_71,
  input  B,
  input  nB,
  input  C,
  input  nC,
  output out_76
);

  wire and_1_out, and_2_out, and_3_out, and_4_out, not_1_out, not_2_out, not_3_out;

  assign in_5 = in_4 ? in_1 : 1'bz;  // Controlled_Buffer controlled_buffer_1
  assign in_11 = in_10 ? in_1 : 1'bz;  // Controlled_Buffer controlled_buffer_2
  assign in_17 = in_16 ? in_1 : 1'bz;  // Controlled_Buffer controlled_buffer_3
  assign in_59 = in_58 ? in_1 : 1'bz;  // Controlled_Buffer controlled_buffer_4
  assign in_65 = in_64 ? in_1 : 1'bz;  // Controlled_Buffer controlled_buffer_5
  assign B = \Ã  ? in_1 : 1'bz;  // Controlled_Buffer controlled_buffer_6
  not not_1 (not_1_out, in_1);
  assign in_22 = in_23 ? not_1_out : 1'bz;  // Controlled_Buffer controlled_buffer_7
  assign in_28 = in_29 ? not_1_out : 1'bz;  // Controlled_Buffer controlled_buffer_8
  assign in_34 = in_35 ? not_1_out : 1'bz;  // Controlled_Buffer controlled_buffer_9
  assign in_40 = in_41 ? not_1_out : 1'bz;  // Controlled_Buffer controlled_buffer_10
  assign in_46 = in_47 ? not_1_out : 1'bz;  // Controlled_Buffer controlled_buffer_11
  assign in_52 = in_53 ? not_1_out : 1'bz;  // Controlled_Buffer controlled_buffer_12
  not not_2 (not_2_out, in_2);
  assign in_5 = in_7 ? not_2_out : 1'bz;  // Controlled_Buffer controlled_buffer_13
  assign in_11 = in_13 ? not_2_out : 1'bz;  // Controlled_Buffer controlled_buffer_14
  assign in_17 = in_19 ? not_2_out : 1'bz;  // Controlled_Buffer controlled_buffer_15
  assign in_22 = in_24 ? in_2 : 1'bz;  // Controlled_Buffer controlled_buffer_16
  assign in_28 = in_30 ? in_2 : 1'bz;  // Controlled_Buffer controlled_buffer_17
  assign in_34 = in_36 ? in_2 : 1'bz;  // Controlled_Buffer controlled_buffer_18
  assign in_40 = in_43 ? not_2_out : 1'bz;  // Controlled_Buffer controlled_buffer_19
  assign in_46 = in_49 ? not_2_out : 1'bz;  // Controlled_Buffer controlled_buffer_20
  assign in_52 = in_55 ? not_2_out : 1'bz;  // Controlled_Buffer controlled_buffer_21
  not not_3 (not_3_out, in_3);
  assign in_5 = in_8 ? in_3 : 1'bz;  // Controlled_Buffer controlled_buffer_22
  assign in_11 = in_14 ? in_3 : 1'bz;  // Controlled_Buffer controlled_buffer_23
  assign in_17 = in_20 ? in_3 : 1'bz;  // Controlled_Buffer controlled_buffer_24
  assign in_59 = in_62 ? in_3 : 1'bz;  // Controlled_Buffer controlled_buffer_25
  assign in_65 = in_68 ? in_3 : 1'bz;  // Controlled_Buffer controlled_buffer_26
  assign B = C ? in_3 : 1'bz;  // Controlled_Buffer controlled_buffer_27
  assign in_22 = in_27 ? not_3_out : 1'bz;  // Controlled_Buffer controlled_buffer_28
  assign in_28 = in_33 ? not_3_out : 1'bz;  // Controlled_Buffer controlled_buffer_29
  assign in_34 = in_39 ? not_3_out : 1'bz;  // Controlled_Buffer controlled_buffer_30
  and and_1 (and_1_out, in_5, in_11, in_17);
  and and_2 (and_2_out, in_22, in_28, in_34);
  and and_3 (and_3_out, in_40, in_46, in_52);
  and and_4 (and_4_out, in_59, in_65, B);
  or or_1 (out_76, and_1_out, and_2_out, and_3_out, and_4_out);

  assign in_6 = in_5;
  assign in_9 = in_5;
  assign in_12 = in_11;
  assign in_15 = in_11;
  assign in_18 = in_17;
  assign in_21 = in_17;
  assign in_25 = in_22;
  assign in_26 = in_22;
  assign in_31 = in_28;
  assign in_32 = in_28;
  assign in_37 = in_34;
  assign in_38 = in_34;
  assign in_42 = in_40;
  assign in_44 = in_40;
  assign in_45 = in_40;
  assign in_48 = in_46;
  assign in_50 = in_46;
  assign in_51 = in_46;
  assign in_54 = in_52;
  assign in_56 = in_52;
  assign in_57 = in_52;
  assign in_60 = in_59;
  assign in_61 = in_59;
  assign in_63 = in_59;
  assign in_66 = in_65;
  assign in_67 = in_65;
  assign in_69 = in_65;
  assign in_71 = B;
  assign nB = B;
  assign nC = B;

  // Notes on the sheet:
  //   A
endmodule
