// Logisim project pal.circ as structural Verilog: 1 circuit, main circuit main
module main (
  input  in_1,
  input  in_2,
  input  in_3,
  input  in_4,
  input  in_5,
  input  in_6,
  input  in_7,
  input  in_8,
  input  in_9,
  input  in_10,
  input  in_11,
  input  in_12,
  input  in_13,
  input  in_14,
  input  in_15,
  input  in_16,
  input  in_17,
  input  in_18,
  input  in_19,
  input  in_20,
  input  A,
  input  \Ã ,
  input  B,
  input  nB,
  input  in_25,
  input  in_26,
  input  in_27,
  input  in_28,
  input  in_29,
  input  in_30,
  input  in_31,
  input  in_32,
  input  in_33,
  input  in_34,
  input  in_35,
  input  in_36,
  input  in_37,
  input  in_38,
  input  in_39,
  input  in_40,
  input  in_41,
  input  in_42,
  input  in_43,
  input  in_44,
  input  in_45,
  input  in_46,
  input  in_47,
  input  in_48,
  input  in_49,
  input  in_50,
  input  in_51,
  input  in_52,
  input  in_53,
  input  in_54,
  input  in_55,
  input  in_56,
  input  in_57,
  input  in_58,
  input  in_59,
  input  in_60,
  input  in_61,
  input  in_62,
  input  in_63,
  input  in_64,
  input  in_65,
  input  in_66,
  input  in_67,
  input  in_68,
  input  in_69,
  input  in_70,
  input  in_71,
  input  in_72,
  input  in_73,
  input  in_74,
  input  in_75,
  input  in_76,
  input  in_77,
  input  in_78,
  input  in_79,
  input  in_80,
  input  in_81,
  input  in_82,
  input  in_83,
  input  in_84,
  input  in_85,
  input  in_86,
  input  in_87,
  input  in_88,
  input  in_89,
  input  in_90,
  input  A_2,
  input  \Ã_2 ,
  input  B_2,
  input  nB_2,
  input  C,
  input  nC,
  output out_97,
  output out_98
);

  wire and_1_out, and_2_out, and_3_out, and_4_out, and_5_out, and_6_out, and_7_out;

  and and_1 (and_1_out, in_1, in_5);
  and and_2 (and_2_out, in_9, in_13);
  and and_3 (and_3_out, in_17, A);
  or or_1 (out_97, and_1_out, and_2_out, and_3_out);
  and and_4 (and_4_out, in_25, in_31, in_37);
  and and_5 (and_5_out, in_43, in_49, in_55);
  and and_6 (and_6_out, in_61, in_67, in_73);
  and and_7 (and_7_out, in_79, in_85, A_2);
  or or_2 (out_98, and_4_out, and_5_out, and_6_out, and_7_out);

  assign B = A;
  assign B_2 = A_2;
  assign C = A_2;
  assign in_2 = in_1;
  assign in_3 = in_1;
  assign in_4 = in_1;
  assign in_6 = in_5;
  assign in_7 = in_5;
  assign in_8 = in_5;
  assign in_10 = in_9;
  assign in_11 = in_9;
  assign in_12 = in_9;
  assign in_15 = in_13;
  assign in_16 = in_13;
  assign in_18 = in_17;
  assign in_19 = in_17;
  assign in_20 = in_17;
  assign in_26 = in_25;
  assign in_27 = in_25;
  assign in_28 = in_25;
  assign in_29 = in_25;
  assign in_30 = in_25;
  assign in_32 = in_31;
  assign in_33 = in_31;
  assign in_34 = in_31;
  assign in_35 = in_31;
  assign in_36 = in_31;
  assign in_38 = in_37;
  assign in_39 = in_37;
  assign in_40 = in_37;
  assign in_41 = in_37;
  assign in_42 = in_37;
  assign in_44 = in_43;
  assign in_45 = in_43;
  assign in_46 = in_43;
  assign in_47 = in_43;
  assign in_48 = in_43;
  assign in_50 = in_49;
  assign in_51 = in_49;
  assign in_52 = in_49;
  assign in_53 = in_49;
  assign in_54 = in_49;
  assign in_56 = in_55;
  assign in_57 = in_55;
  assign in_58 = in_55;
  assign in_59 = in_55;
  assign in_60 = in_55;
  assign in_62 = in_61;
  assign in_63 = in_61;
  assign in_64 = in_61;
  assign in_65 = in_61;
  assign in_66 = in_61;
  assign in_68 = in_67;
  assign in_69 = in_67;
  assign in_70 = in_67;
  assign in_71 = in_67;
  assign in_72 = in_67;
  assign in_74 = in_73;
  assign in_75 = in_73;
  assign in_76 = in_73;
  assign in_77 = in_73;
  assign in_78 = in_73;
  assign in_80 = in_79;
  assign in_81 = in_79;
  assign in_82 = in_79;
  assign in_83 = in_79;
  assign in_84 = in_79;
  assign in_86 = in_85;
  assign in_87 = in_85;
  assign in_88 = in_85;
  assign in_89 = in_85;
  assign in_90 = in_85;
  assign nB = A;
  assign nB_2 = A_2;
  assign nC = A_2;
  assign \Ã  = A;
  assign \Ã_2  = A_2;
endmodule
