// Logisim project memoriaram.circ as structural Verilog: 1 circuit, main circuit main
module main (
  input  in_1,
  input  in_2,
  input  [7:0] ENTRADA_DADOS,
  input  [23:0] in_4,
  input  END_MEMORIA,
  input  in_6,
  input  in_7,
  input  [4:0] in_8,
  input  in_9,
  input  in_10,
  input  in_11,
  input  in_12,
  input  LD,
  input  CLR,
  input  LD_2,
  input  CLR_2,
  output [7:0] PINO_DE_ANALISE,
  output [23:0] out_18,
  output [7:0] PINO_DE_ANALISE_2,
  output [23:0] out_20
);

  wire clock_1_out, clock_2_out;

  assign PINO_DE_ANALISE_2 = in_9 ? PINO_DE_ANALISE : 8'bz;  // Controlled_Buffer controlled_buffer_1
  assign PINO_DE_ANALISE = in_10 ? PINO_DE_ANALISE_2 : 8'bz;  // Controlled_Buffer controlled_buffer_2
  assign PINO_DE_ANALISE = in_1 ? ENTRADA_DADOS : 8'bz;  // Controlled_Buffer controlled_buffer_3
  Clock clock_1 (.out(clock_1_out));
  RAM #(.addrWidth(3)) ram_1 (
    .addr({END_MEMORIA, in_6, in_7}), .data(PINO_DE_ANALISE_2), .sel(1'b1), .clk(clock_1_out), .ld(LD),
    .clr(CLR));
  assign out_18 = in_12 ? out_20 : 24'bz;  // Controlled_Buffer controlled_buffer_4
  assign out_20 = in_11 ? out_18 : 24'bz;  // Controlled_Buffer controlled_buffer_5
  assign out_18 = in_2 ? in_4 : 24'bz;  // Controlled_Buffer controlled_buffer_6
  Clock clock_2 (.out(clock_2_out));
  RAM #(.addrWidth(5), .dataWidth(24)) ram_2 (
    .addr(in_8), .data(out_20), .sel(1'b1), .clk(clock_2_out), .ld(LD_2), .clr(CLR_2));

  // Notes on the sheet:
  //   PINO DE CONTROLE
  //   PINOS DE CONTROLE
  //   FONTE DE ENERGIA
  //   CLK
  //   PINO DE ANALISE
  //   PINO DE CONTROLE
  //   END MEMORIA
  //   PINOS DE CONTROLE
  //   SEGUNDA MEMORIA
  //   FONTE DE ENERGIA
  //   ENTRADA DADOS
  //   CLK
  //   PINO DE ANALISE
endmodule
