// Logisim project memoriarom.circ as structural Verilog: 1 circuit, main circuit main
module main (
  input  [2:0] ENDERECO,
  input  [4:0] ENDERECO_2,
  input  in_3,
  input  in_4
);

  wire [3:0] rom_2_data, rom_2_data_2, rom_2_data_3, rom_2_data_4;
  wire [7:0] rom_1_data;

  Hex_Digit_Display hex_digit_display_1 (.value(rom_1_data[7:4]));  // open: dp
  ROM #(.addrWidth(3)) rom_1 (.addr(ENDERECO), .data(rom_1_data), .sel(in_3));
  Hex_Digit_Display hex_digit_display_2 (.value(rom_1_data[3:0]));  // open: dp
  Hex_Digit_Display hex_digit_display_3 (.value(rom_2_data_4));  // open: dp
  ROM #(.addrWidth(5), .dataWidth(16)) rom_2 (
    .addr(ENDERECO_2), .data({rom_2_data_4, rom_2_data_3, rom_2_data_2, rom_2_data}), .sel(in_4));
  Hex_Digit_Display hex_digit_display_4 (.value(rom_2_data_3));  // open: dp
  Hex_Digit_Display hex_digit_display_5 (.value(rom_2_data));  // open: dp
  Hex_Digit_Display hex_digit_display_6 (.value(rom_2_data_2));  // open: dp

  // Notes on the sheet:
  //   contents of rom_1 (hex, n*v repeats v):
  //   0 a 0 55 0 5 0 17
  //   DISPLAYS
  //   SEGUNDA MEMORIA
  //   contents of rom_2 (hex, n*v repeats v):
  //   1234 a 0 55 0 5 0 17
  //   DISPLAYS
endmodule
