// Logisim project LTU.circ as structural Verilog: 1 circuit, main circuit main
module main (
  input  A2,
  input  in_2,
  input  in_3,
  input  in_4,
  input  A1,
  input  in_6,
  input  in_7,
  input  in_8,
  input  A0,
  input  in_10,
  input  in_11,
  output out_12
);

  wire and_1_out, and_2_out, and_3_out, and_4_out, and_5_out, and_6_out, and_7_out, and_8_out, and_9_out,
       and_10_out, and_11_out, and_12_out, and_13_out, and_14_out, clock_1_out, controlled_buffer_1_out,
       controlled_buffer_2_out, controlled_buffer_3_out, controlled_buffer_4_out, controlled_buffer_5_out,
       controlled_buffer_6_out, controlled_buffer_7_out, d_ff_1_q, d_ff_2_q, d_ff_3_q, d_ff_4_q, d_ff_5_q,
       d_ff_6_q, d_ff_7_q, not_1_out, not_2_out, not_3_out, not_4_out, not_5_out, not_6_out, not_7_out,
       not_8_out, not_9_out, not_10_out, not_11_out;

  not not_1 (not_1_out, A2);
  not not_2 (not_2_out, A1);
  not not_3 (not_3_out, A0);
  not not_4 (not_4_out, A2);
  not not_5 (not_5_out, A1);
  not not_6 (not_6_out, A2);
  not not_7 (not_7_out, A0);
  not not_8 (not_8_out, A2);
  not not_9 (not_9_out, A1);
  not not_10 (not_10_out, A0);
  not not_11 (not_11_out, A0);
  and and_1 (and_1_out, not_1_out, not_2_out, not_3_out);
  and and_2 (and_2_out, not_4_out, not_5_out, A0);
  and and_3 (and_3_out, not_6_out, A1, not_7_out);
  and and_4 (and_4_out, not_8_out, A1, A0);
  and and_5 (and_5_out, A2, not_9_out, not_10_out);
  and and_6 (and_6_out, A2, A1, not_11_out);
  and and_7 (and_7_out, A2, A1, A0);
  assign controlled_buffer_1_out = in_2 ? and_1_out : 1'bz;  // Controlled_Buffer controlled_buffer_1
  assign controlled_buffer_2_out = in_3 ? and_2_out : 1'bz;  // Controlled_Buffer controlled_buffer_2
  assign controlled_buffer_3_out = in_4 ? and_3_out : 1'bz;  // Controlled_Buffer controlled_buffer_3
  assign controlled_buffer_4_out = in_6 ? and_4_out : 1'bz;  // Controlled_Buffer controlled_buffer_4
  assign controlled_buffer_5_out = in_7 ? and_5_out : 1'bz;  // Controlled_Buffer controlled_buffer_5
  assign controlled_buffer_6_out = in_8 ? and_6_out : 1'bz;  // Controlled_Buffer controlled_buffer_6
  assign controlled_buffer_7_out = in_10 ? and_7_out : 1'bz;  // Controlled_Buffer controlled_buffer_7
  and and_8 (and_8_out, controlled_buffer_1_out, in_11);
  and and_9 (and_9_out, controlled_buffer_2_out, in_11);
  and and_10 (and_10_out, controlled_buffer_3_out, in_11);
  and and_11 (and_11_out, controlled_buffer_4_out, in_11);
  and and_12 (and_12_out, controlled_buffer_5_out, in_11);
  and and_13 (and_13_out, controlled_buffer_6_out, in_11);
  and and_14 (and_14_out, controlled_buffer_7_out, in_11);
  Clock clock_1 (.out(clock_1_out));
  D_Flip_Flop d_ff_1 (.clk(clock_1_out), .D(and_8_out), .Q(d_ff_1_q));  // open: Qn, preset, en, reset
  D_Flip_Flop d_ff_2 (.clk(clock_1_out), .D(and_9_out), .Q(d_ff_2_q));  // open: Qn, preset, en, reset
  D_Flip_Flop d_ff_3 (.clk(clock_1_out), .D(and_10_out), .Q(d_ff_3_q));  // open: Qn, preset, en, reset
  D_Flip_Flop d_ff_4 (.clk(clock_1_out), .D(and_11_out), .Q(d_ff_4_q));  // open: Qn, preset, en, reset
  D_Flip_Flop d_ff_5 (.clk(clock_1_out), .D(and_12_out), .Q(d_ff_5_q));  // open: Qn, preset, en, reset
  D_Flip_Flop d_ff_6 (.clk(clock_1_out), .D(and_13_out), .Q(d_ff_6_q));  // open: Qn, preset, en, reset
  D_Flip_Flop d_ff_7 (.clk(clock_1_out), .D(and_14_out), .Q(d_ff_7_q));  // open: Qn, preset, en, reset
  or or_1 (out_12, d_ff_1_q, d_ff_2_q, d_ff_3_q, d_ff_4_q, d_ff_5_q, d_ff_6_q, d_ff_7_q);
endmodule
