// Logisim project lut.circ as structural Verilog: 1 circuit, main circuit main
module main (
  input  A3,
  input  in_2,
  input  in_3,
  input  in_4,
  input  A2,
  input  in_6,
  input  in_7,
  input  in_8,
  input  in_9,
  input  in_10,
  input  in_11,
  input  in_12,
  input  in_13,
  input  in_14,
  input  A1,
  input  in_16,
  input  in_17,
  input  in_18,
  input  in_19,
  input  in_20,
  input  in_21,
  input  in_22,
  input  in_23,
  input  in_24,
  input  A0,
  input  in_26,
  input  in_27,
  input  in_28,
  input  in_29,
  input  in_30,
  input  in_31,
  input  in_32,
  input  in_33,
  input  in_34,
  input  in_35,
  input  in_36,
  input  in_37,
  input  in_38,
  input  in_39,
  input  in_40,
  input  in_41,
  input  in_42,
  input  in_43,
  input  in_44,
  input  in_45,
  input  in_46,
  input  in_47,
  input  in_48,
  input  in_49,
  input  in_50,
  input  in_51,
  input  in_52,
  input  in_53,
  input  in_54,
  input  in_55,
  input  in_56,
  input  in_57,
  input  in_58,
  input  in_59,
  input  in_60,
  input  in_61,
  input  in_62,
  input  in_63,
  input  in_64,
  input  in_65,
  input  in_66,
  input  in_67,
  input  in_68,
  input  in_69,
  input  in_70,
  input  in_71,
  input  [3:0] in_72,
  input  [3:0] in_73,
  input  in_74,
  input  in_75,
  input  in_76,
  input  in_77,
  input  in_78,
  input  in_79,
  input  in_80,
  input  in_81,
  input  in_82,
  input  in_83,
  input  in_84,
  input  in_85,
  input  in_86,
  input  in_87,
  input  in_88,
  input  in_89,
  input  [3:0] in_90,
  input  [3:0] in_91,
  input  in_92,
  input  in_93,
  input  in_94,
  input  in_95,
  input  in_96,
  input  in_97,
  input  in_98,
  input  in_99,
  input  in_100,
  input  in_101,
  input  IN,
  input  in_103,
  output out_104,
  output out_105,
  output out_106,
  output [3:0] out_107,
  output out_108
);

  wire _0000_out, _0001_out, _0010_out, _0011_out, _0100_out, _0101_out, _0110_2_out, _0110_out, _0111_out,
       and_9_out, and_10_out, controlled_buffer_1_out, controlled_buffer_2_out, controlled_buffer_3_out,
       controlled_buffer_4_out, controlled_buffer_5_out, controlled_buffer_6_out, controlled_buffer_7_out,
       controlled_buffer_8_out, controlled_buffer_9_out, controlled_buffer_10_out, controlled_buffer_11_out,
       controlled_buffer_12_out, controlled_buffer_13_out, controlled_buffer_14_out,
       controlled_buffer_15_out, controlled_buffer_16_out, controlled_buffer_17_out,
       controlled_buffer_18_out, controlled_buffer_19_out, controlled_buffer_20_out,
       controlled_buffer_21_out, controlled_buffer_22_out, controlled_buffer_23_out,
       controlled_buffer_24_out, controlled_buffer_25_out, controlled_buffer_26_out,
       controlled_buffer_27_out, controlled_buffer_28_out, controlled_buffer_29_out,
       controlled_buffer_30_out, controlled_buffer_31_out, controlled_buffer_32_out,
       controlled_buffer_33_out, controlled_buffer_34_out, controlled_buffer_35_out,
       controlled_buffer_36_out, controlled_buffer_37_out, controlled_buffer_38_out,
       controlled_buffer_39_out, controlled_buffer_41_out, demultiplexer_1_out0, demultiplexer_1_out1,
       demultiplexer_1_out2, demultiplexer_1_out3, demultiplexer_1_out4, demultiplexer_1_out5,
       demultiplexer_1_out6, demultiplexer_1_out7, demultiplexer_1_out8, demultiplexer_1_out9,
       demultiplexer_1_out10, demultiplexer_1_out11, demultiplexer_1_out12, demultiplexer_1_out13,
       demultiplexer_1_out14, demultiplexer_1_out15, demultiplexer_2_out0, demultiplexer_2_out1,
       demultiplexer_2_out2, demultiplexer_2_out3, demultiplexer_2_out4, demultiplexer_2_out5,
       demultiplexer_2_out6, demultiplexer_2_out7, demultiplexer_2_out8, demultiplexer_2_out9,
       demultiplexer_2_out10, demultiplexer_2_out11, demultiplexer_2_out12, demultiplexer_2_out13,
       demultiplexer_2_out14, demultiplexer_2_out15, demultiplexer_3_out0, demultiplexer_3_out1,
       demultiplexer_3_out2, demultiplexer_3_out3, demultiplexer_3_out4, demultiplexer_3_out5,
       demultiplexer_3_out6, demultiplexer_3_out7, demultiplexer_3_out8, demultiplexer_3_out9,
       demultiplexer_3_out10, demultiplexer_3_out11, demultiplexer_3_out12, demultiplexer_3_out13,
       demultiplexer_3_out14, demultiplexer_3_out15, demultiplexer_7_out0, demultiplexer_7_out1,
       demultiplexer_7_out2, demultiplexer_7_out3, demultiplexer_7_out4, demultiplexer_7_out5,
       demultiplexer_7_out6, demultiplexer_7_out7, demultiplexer_7_out8, demultiplexer_7_out9,
       demultiplexer_7_out10, demultiplexer_7_out11, demultiplexer_7_out12, demultiplexer_7_out13,
       demultiplexer_7_out14, demultiplexer_7_out15, demultiplexer_8_out0, demultiplexer_8_out1,
       demultiplexer_8_out2, demultiplexer_8_out3, demultiplexer_8_out4, demultiplexer_8_out5,
       demultiplexer_8_out6, demultiplexer_8_out7, demultiplexer_8_out8, demultiplexer_8_out9,
       demultiplexer_8_out10, demultiplexer_8_out11, demultiplexer_8_out12, demultiplexer_8_out13,
       demultiplexer_8_out14, demultiplexer_8_out15, demultiplexer_9_out0, demultiplexer_9_out1,
       demultiplexer_9_out2, demultiplexer_9_out3, demultiplexer_9_out4, demultiplexer_9_out5,
       demultiplexer_9_out6, demultiplexer_9_out7, demultiplexer_9_out8, demultiplexer_9_out9,
       demultiplexer_9_out10, demultiplexer_9_out11, demultiplexer_9_out12, demultiplexer_9_out13,
       demultiplexer_9_out14, demultiplexer_9_out15, demultiplexer_12_out0, demultiplexer_12_out1,
       demultiplexer_12_out2, demultiplexer_12_out3, demultiplexer_12_out4, demultiplexer_12_out5,
       demultiplexer_12_out6, demultiplexer_12_out7, demultiplexer_12_out8, demultiplexer_12_out9,
       demultiplexer_12_out10, demultiplexer_12_out11, demultiplexer_12_out12, demultiplexer_12_out13,
       demultiplexer_12_out14, demultiplexer_12_out15, demultiplexer_13_out0, demultiplexer_13_out1,
       demultiplexer_13_out2, demultiplexer_13_out3, demultiplexer_13_out4, demultiplexer_13_out5,
       demultiplexer_13_out6, demultiplexer_13_out7, demultiplexer_13_out8, demultiplexer_13_out9,
       demultiplexer_13_out10, demultiplexer_13_out11, demultiplexer_13_out12, demultiplexer_13_out13,
       demultiplexer_13_out14, demultiplexer_13_out15, demultiplexer_14_out0, demultiplexer_14_out1,
       demultiplexer_14_out2, demultiplexer_14_out3, demultiplexer_14_out4, demultiplexer_14_out5,
       demultiplexer_14_out6, demultiplexer_14_out7, demultiplexer_14_out8, demultiplexer_14_out9,
       demultiplexer_14_out10, demultiplexer_14_out11, demultiplexer_14_out12, demultiplexer_14_out13,
       demultiplexer_14_out14, demultiplexer_14_out15, not_5_out;
  wire [3:0] and_1_out, and_2_out, and_3_out, and_4_out, and_5_out, and_6_out, and_7_out, and_8_out,
       not_1_out, not_2_out, not_3_out, not_4_out, or_1_out, or_2_out, or_3_out, or_4_out, or_5_out,
       undriven, undriven_2, undriven_3, undriven_4, undriven_5, undriven_6;

  assign and_1_out = or_1_out & undriven;  // AND_Gate and_1, 4 bits wide
  assign or_1_out = and_2_out | and_4_out;  // OR_Gate or_1, 4 bits wide
  assign and_2_out = in_91 & undriven_2;  // AND_Gate and_2, 4 bits wide
  assign or_2_out = and_1_out | and_3_out;  // OR_Gate or_2, 4 bits wide
  assign and_3_out = in_73 & not_1_out;  // AND_Gate and_3, 4 bits wide
  assign not_1_out = ~undriven;  // NOT_Gate not_1, 4 bits wide
  assign and_4_out = in_91 & not_2_out;  // AND_Gate and_4, 4 bits wide
  assign not_2_out = ~undriven_2;  // NOT_Gate not_2, 4 bits wide
  assign or_3_out = or_2_out;  // OR_Gate or_3, 4 bits wide OR_Gate
  Demultiplexer #(.select(4), .enable("false")) demultiplexer_1 (
    .out0(demultiplexer_1_out0), .out1(demultiplexer_1_out1), .out2(demultiplexer_1_out2),
    .out3(demultiplexer_1_out3), .out4(demultiplexer_1_out4), .out5(demultiplexer_1_out5),
    .out6(demultiplexer_1_out6), .out7(demultiplexer_1_out7), .out8(demultiplexer_1_out8),
    .out9(demultiplexer_1_out9), .out10(demultiplexer_1_out10), .out11(demultiplexer_1_out11),
    .out12(demultiplexer_1_out12), .out13(demultiplexer_1_out13), .out14(demultiplexer_1_out14),
    .out15(demultiplexer_1_out15), .in(in_39), .sel({in_58, in_59, in_60, in_61}));
  Demultiplexer #(.select(4), .enable("false")) demultiplexer_2 (
    .out0(demultiplexer_2_out0), .out1(demultiplexer_2_out1), .out2(demultiplexer_2_out2),
    .out3(demultiplexer_2_out3), .out4(demultiplexer_2_out4), .out5(demultiplexer_2_out5),
    .out6(demultiplexer_2_out6), .out7(demultiplexer_2_out7), .out8(demultiplexer_2_out8),
    .out9(demultiplexer_2_out9), .out10(demultiplexer_2_out10), .out11(demultiplexer_2_out11),
    .out12(demultiplexer_2_out12), .out13(demultiplexer_2_out13), .out14(demultiplexer_2_out14),
    .out15(demultiplexer_2_out15), .in(in_67), .sel(undriven));
  Demultiplexer #(.select(4), .enable("false")) demultiplexer_3 (
    .out0(demultiplexer_3_out0), .out1(demultiplexer_3_out1), .out2(demultiplexer_3_out2),
    .out3(demultiplexer_3_out3), .out4(demultiplexer_3_out4), .out5(demultiplexer_3_out5),
    .out6(demultiplexer_3_out6), .out7(demultiplexer_3_out7), .out8(demultiplexer_3_out8),
    .out9(demultiplexer_3_out9), .out10(demultiplexer_3_out10), .out11(demultiplexer_3_out11),
    .out12(demultiplexer_3_out12), .out13(demultiplexer_3_out13), .out14(demultiplexer_3_out14),
    .out15(demultiplexer_3_out15), .in(in_85), .sel(undriven_2));
  Demultiplexer #(.select(4), .enable("false")) demultiplexer_4 (
    .out0(demultiplexer_3_out0), .out1(demultiplexer_3_out1), .out2(demultiplexer_3_out2),
    .out3(demultiplexer_3_out3), .out4(demultiplexer_3_out4), .out5(demultiplexer_3_out5),
    .out6(demultiplexer_3_out6), .out7(demultiplexer_3_out7), .out8(demultiplexer_3_out8),
    .out9(demultiplexer_3_out9), .out10(demultiplexer_3_out10), .out11(demultiplexer_3_out11),
    .out12(demultiplexer_3_out12), .out13(demultiplexer_3_out13), .out14(demultiplexer_3_out14),
    .out15(demultiplexer_3_out15), .in(in_87), .sel({in_99, in_98, in_97, in_96}));
  and _0000 (_0000_out, ~A3, ~A2, ~A1, ~A0);  // AND_Gate
  and _0001 (_0001_out, ~A3, ~A2, ~A1, A0);  // AND_Gate
  and _0010 (_0010_out, ~A3, ~A2, A1, ~A0);  // AND_Gate
  and _0011 (_0011_out, ~A3, ~A2, A1, A0);  // AND_Gate
  and _0100 (_0100_out, ~A3, A2, ~A1, ~A0);  // AND_Gate
  and _0101 (_0101_out, ~A3, A2, ~A1, A0);  // AND_Gate
  and _0110 (_0110_out, ~A3, A2, A1, ~A0);  // AND_Gate
  and _0111 (_0111_out, ~A3, A2, A1, A0);  // AND_Gate
  and _0110_2 (_0110_2_out, A3, ~A2, ~A1, A0);  // AND_Gate
  Demultiplexer #(.select(4), .enable("false")) demultiplexer_5 (
    .out0(demultiplexer_1_out0), .out1(demultiplexer_1_out1), .out2(demultiplexer_1_out2),
    .out3(demultiplexer_1_out3), .out4(demultiplexer_1_out4), .out5(demultiplexer_1_out5),
    .out6(demultiplexer_1_out6), .out7(demultiplexer_1_out7), .out8(demultiplexer_1_out8),
    .out9(demultiplexer_1_out9), .out10(demultiplexer_1_out10), .out11(demultiplexer_1_out11),
    .out12(demultiplexer_1_out12), .out13(demultiplexer_1_out13), .out14(demultiplexer_1_out14),
    .out15(demultiplexer_1_out15), .in(in_44), .sel({in_65, in_64, in_63, in_62}));
  Demultiplexer #(.select(4), .enable("false")) demultiplexer_6 (
    .out0(demultiplexer_2_out0), .out1(demultiplexer_2_out1), .out2(demultiplexer_2_out2),
    .out3(demultiplexer_2_out3), .out4(demultiplexer_2_out4), .out5(demultiplexer_2_out5),
    .out6(demultiplexer_2_out6), .out7(demultiplexer_2_out7), .out8(demultiplexer_2_out8),
    .out9(demultiplexer_2_out9), .out10(demultiplexer_2_out10), .out11(demultiplexer_2_out11),
    .out12(demultiplexer_2_out12), .out13(demultiplexer_2_out13), .out14(demultiplexer_2_out14),
    .out15(demultiplexer_2_out15), .in(in_70), .sel({in_83, in_82, in_81, in_80}));
  assign controlled_buffer_1_out = in_7 ? _0000_out : 1'bz;  // Controlled_Buffer controlled_buffer_1
  assign controlled_buffer_2_out = in_9 ? _0001_out : 1'bz;  // Controlled_Buffer controlled_buffer_2
  assign controlled_buffer_3_out = in_12 ? _0010_out : 1'bz;  // Controlled_Buffer controlled_buffer_3
  assign controlled_buffer_4_out = in_16 ? _0011_out : 1'bz;  // Controlled_Buffer controlled_buffer_4
  assign controlled_buffer_5_out = in_19 ? _0100_out : 1'bz;  // Controlled_Buffer controlled_buffer_5
  assign controlled_buffer_6_out = in_22 ? _0101_out : 1'bz;  // Controlled_Buffer controlled_buffer_6
  assign controlled_buffer_7_out = in_24 ? _0110_out : 1'bz;  // Controlled_Buffer controlled_buffer_7
  assign controlled_buffer_8_out = in_31 ? _0111_out : 1'bz;  // Controlled_Buffer controlled_buffer_8
  assign controlled_buffer_9_out = in_34 ? _0110_2_out : 1'bz;  // Controlled_Buffer controlled_buffer_9
  assign and_5_out = or_5_out & undriven_4;  // AND_Gate and_5, 4 bits wide
  assign and_6_out = in_90 & undriven_3;  // AND_Gate and_6, 4 bits wide
  assign or_4_out = and_5_out | and_8_out;  // OR_Gate or_4, 4 bits wide
  assign or_5_out = and_6_out | and_7_out;  // OR_Gate or_5, 4 bits wide
  assign and_7_out = in_90 & not_4_out;  // AND_Gate and_7, 4 bits wide
  or or_6 (out_105, controlled_buffer_9_out, controlled_buffer_1_out, controlled_buffer_2_out, controlled_buffer_3_out, controlled_buffer_5_out, controlled_buffer_6_out, controlled_buffer_7_out, controlled_buffer_8_out);
  Demultiplexer #(.select(4), .enable("false")) demultiplexer_7 (
    .out0(demultiplexer_7_out0), .out1(demultiplexer_7_out1), .out2(demultiplexer_7_out2),
    .out3(demultiplexer_7_out3), .out4(demultiplexer_7_out4), .out5(demultiplexer_7_out5),
    .out6(demultiplexer_7_out6), .out7(demultiplexer_7_out7), .out8(demultiplexer_7_out8),
    .out9(demultiplexer_7_out9), .out10(demultiplexer_7_out10), .out11(demultiplexer_7_out11),
    .out12(demultiplexer_7_out12), .out13(demultiplexer_7_out13), .out14(demultiplexer_7_out14),
    .out15(demultiplexer_7_out15), .in(in_36), .sel({in_52, in_53, in_54, in_55}));
  assign and_8_out = in_72 & not_3_out;  // AND_Gate and_8, 4 bits wide
  assign not_3_out = ~undriven_4;  // NOT_Gate not_3, 4 bits wide
  assign not_4_out = ~undriven_3;  // NOT_Gate not_4, 4 bits wide
  assign out_107 = or_3_out | or_4_out;  // OR_Gate or_7, 4 bits wide
  Demultiplexer #(.select(4), .enable("false")) demultiplexer_8 (
    .out0(demultiplexer_8_out0), .out1(demultiplexer_8_out1), .out2(demultiplexer_8_out2),
    .out3(demultiplexer_8_out3), .out4(demultiplexer_8_out4), .out5(demultiplexer_8_out5),
    .out6(demultiplexer_8_out6), .out7(demultiplexer_8_out7), .out8(demultiplexer_8_out8),
    .out9(demultiplexer_8_out9), .out10(demultiplexer_8_out10), .out11(demultiplexer_8_out11),
    .out12(demultiplexer_8_out12), .out13(demultiplexer_8_out13), .out14(demultiplexer_8_out14),
    .out15(demultiplexer_8_out15), .in(in_84), .sel(undriven_3));
  Demultiplexer #(.select(4), .enable("false")) demultiplexer_9 (
    .out0(demultiplexer_9_out0), .out1(demultiplexer_9_out1), .out2(demultiplexer_9_out2),
    .out3(demultiplexer_9_out3), .out4(demultiplexer_9_out4), .out5(demultiplexer_9_out5),
    .out6(demultiplexer_9_out6), .out7(demultiplexer_9_out7), .out8(demultiplexer_9_out8),
    .out9(demultiplexer_9_out9), .out10(demultiplexer_9_out10), .out11(demultiplexer_9_out11),
    .out12(demultiplexer_9_out12), .out13(demultiplexer_9_out13), .out14(demultiplexer_9_out14),
    .out15(demultiplexer_9_out15), .in(in_66), .sel(undriven_4));
  assign controlled_buffer_10_out = in_35 ? demultiplexer_7_out0 : 1'bz;  // Controlled_Buffer controlled_buffer_10
  assign controlled_buffer_11_out = in_37 ? demultiplexer_7_out1 : 1'bz;  // Controlled_Buffer controlled_buffer_11
  assign controlled_buffer_12_out = in_38 ? demultiplexer_7_out2 : 1'bz;  // Controlled_Buffer controlled_buffer_12
  assign controlled_buffer_13_out = in_40 ? demultiplexer_7_out3 : 1'bz;  // Controlled_Buffer controlled_buffer_13
  assign controlled_buffer_14_out = in_41 ? demultiplexer_7_out4 : 1'bz;  // Controlled_Buffer controlled_buffer_14
  assign controlled_buffer_15_out = in_42 ? demultiplexer_7_out5 : 1'bz;  // Controlled_Buffer controlled_buffer_15
  assign controlled_buffer_16_out = in_45 ? demultiplexer_7_out7 : 1'bz;  // Controlled_Buffer controlled_buffer_16
  assign controlled_buffer_17_out = in_46 ? demultiplexer_7_out8 : 1'bz;  // Controlled_Buffer controlled_buffer_17
  assign controlled_buffer_18_out = in_47 ? demultiplexer_7_out9 : 1'bz;  // Controlled_Buffer controlled_buffer_18
  assign controlled_buffer_19_out = in_48 ? demultiplexer_7_out10 : 1'bz;  // Controlled_Buffer controlled_buffer_19
  assign controlled_buffer_20_out = in_49 ? demultiplexer_7_out11 : 1'bz;  // Controlled_Buffer controlled_buffer_20
  assign controlled_buffer_21_out = in_50 ? demultiplexer_7_out12 : 1'bz;  // Controlled_Buffer controlled_buffer_21
  assign controlled_buffer_22_out = in_51 ? demultiplexer_7_out13 : 1'bz;  // Controlled_Buffer controlled_buffer_22
  assign controlled_buffer_23_out = in_56 ? demultiplexer_7_out14 : 1'bz;  // Controlled_Buffer controlled_buffer_23
  assign controlled_buffer_24_out = in_57 ? demultiplexer_7_out15 : 1'bz;  // Controlled_Buffer controlled_buffer_24
  Demultiplexer #(.select(4), .enable("false")) demultiplexer_10 (
    .out0(demultiplexer_9_out0), .out1(demultiplexer_9_out1), .out2(demultiplexer_9_out2),
    .out3(demultiplexer_9_out3), .out4(demultiplexer_9_out4), .out5(demultiplexer_9_out5),
    .out6(demultiplexer_9_out6), .out7(demultiplexer_9_out7), .out8(demultiplexer_9_out8),
    .out9(demultiplexer_9_out9), .out10(demultiplexer_9_out10), .out11(demultiplexer_9_out11),
    .out12(demultiplexer_9_out12), .out13(demultiplexer_9_out13), .out14(demultiplexer_9_out14),
    .out15(demultiplexer_9_out15), .in(in_69), .sel({in_79, in_78, in_77, in_76}));
  Demultiplexer #(.select(4), .enable("false")) demultiplexer_11 (
    .out0(demultiplexer_8_out0), .out1(demultiplexer_8_out1), .out2(demultiplexer_8_out2),
    .out3(demultiplexer_8_out3), .out4(demultiplexer_8_out4), .out5(demultiplexer_8_out5),
    .out6(demultiplexer_8_out6), .out7(demultiplexer_8_out7), .out8(demultiplexer_8_out8),
    .out9(demultiplexer_8_out9), .out10(demultiplexer_8_out10), .out11(demultiplexer_8_out11),
    .out12(demultiplexer_8_out12), .out13(demultiplexer_8_out13), .out14(demultiplexer_8_out14),
    .out15(demultiplexer_8_out15), .in(in_86), .sel({in_95, in_94, in_93, in_92}));
  assign controlled_buffer_25_out = in_43 ? demultiplexer_7_out6 : 1'bz;  // Controlled_Buffer controlled_buffer_25
  Demultiplexer #(.select(4), .enable("false")) demultiplexer_12 (
    .out0(demultiplexer_12_out0), .out1(demultiplexer_12_out1), .out2(demultiplexer_12_out2),
    .out3(demultiplexer_12_out3), .out4(demultiplexer_12_out4), .out5(demultiplexer_12_out5),
    .out6(demultiplexer_12_out6), .out7(demultiplexer_12_out7), .out8(demultiplexer_12_out8),
    .out9(demultiplexer_12_out9), .out10(demultiplexer_12_out10), .out11(demultiplexer_12_out11),
    .out12(demultiplexer_12_out12), .out13(demultiplexer_12_out13), .out14(demultiplexer_12_out14),
    .out15(demultiplexer_12_out15), .in(in_3), .sel({in_27, in_28, in_29, in_30}));
  or or_8 (out_106, controlled_buffer_10_out, controlled_buffer_11_out, controlled_buffer_12_out, controlled_buffer_13_out, controlled_buffer_14_out, controlled_buffer_15_out, controlled_buffer_25_out, controlled_buffer_16_out, controlled_buffer_17_out, controlled_buffer_18_out, controlled_buffer_19_out, controlled_buffer_20_out, controlled_buffer_21_out, controlled_buffer_22_out, controlled_buffer_23_out, controlled_buffer_24_out);
  assign controlled_buffer_26_out = in_2 ? demultiplexer_12_out0 : 1'bz;  // Controlled_Buffer controlled_buffer_26
  assign controlled_buffer_27_out = in_4 ? demultiplexer_12_out1 : 1'bz;  // Controlled_Buffer controlled_buffer_27
  assign controlled_buffer_28_out = in_6 ? demultiplexer_12_out2 : 1'bz;  // Controlled_Buffer controlled_buffer_28
  assign controlled_buffer_29_out = in_8 ? demultiplexer_12_out3 : 1'bz;  // Controlled_Buffer controlled_buffer_29
  assign controlled_buffer_30_out = in_10 ? demultiplexer_12_out4 : 1'bz;  // Controlled_Buffer controlled_buffer_30
  assign controlled_buffer_31_out = in_11 ? demultiplexer_12_out5 : 1'bz;  // Controlled_Buffer controlled_buffer_31
  assign controlled_buffer_32_out = in_14 ? demultiplexer_12_out7 : 1'bz;  // Controlled_Buffer controlled_buffer_32
  assign controlled_buffer_33_out = in_17 ? demultiplexer_12_out8 : 1'bz;  // Controlled_Buffer controlled_buffer_33
  assign controlled_buffer_34_out = in_18 ? demultiplexer_12_out9 : 1'bz;  // Controlled_Buffer controlled_buffer_34
  assign controlled_buffer_35_out = in_20 ? demultiplexer_12_out10 : 1'bz;  // Controlled_Buffer controlled_buffer_35
  assign controlled_buffer_36_out = in_21 ? demultiplexer_12_out11 : 1'bz;  // Controlled_Buffer controlled_buffer_36
  assign controlled_buffer_37_out = in_23 ? demultiplexer_12_out12 : 1'bz;  // Controlled_Buffer controlled_buffer_37
  assign controlled_buffer_38_out = in_26 ? demultiplexer_12_out13 : 1'bz;  // Controlled_Buffer controlled_buffer_38
  assign controlled_buffer_39_out = in_32 ? demultiplexer_12_out14 : 1'bz;  // Controlled_Buffer controlled_buffer_39
  assign demultiplexer_12_out15 = in_33 ? demultiplexer_12_out15 : 1'bz;  // Controlled_Buffer controlled_buffer_40
  assign controlled_buffer_41_out = in_13 ? demultiplexer_12_out6 : 1'bz;  // Controlled_Buffer controlled_buffer_41
  or or_9 (out_104, controlled_buffer_26_out, controlled_buffer_27_out, controlled_buffer_28_out, controlled_buffer_29_out, controlled_buffer_30_out, controlled_buffer_31_out, controlled_buffer_41_out, controlled_buffer_32_out, controlled_buffer_33_out, controlled_buffer_34_out, controlled_buffer_35_out, controlled_buffer_36_out, controlled_buffer_37_out, controlled_buffer_38_out, controlled_buffer_39_out, demultiplexer_12_out15);
  Demultiplexer #(.select(4), .enable("false")) demultiplexer_13 (
    .out0(demultiplexer_13_out0), .out1(demultiplexer_13_out1), .out2(demultiplexer_13_out2),
    .out3(demultiplexer_13_out3), .out4(demultiplexer_13_out4), .out5(demultiplexer_13_out5),
    .out6(demultiplexer_13_out6), .out7(demultiplexer_13_out7), .out8(demultiplexer_13_out8),
    .out9(demultiplexer_13_out9), .out10(demultiplexer_13_out10), .out11(demultiplexer_13_out11),
    .out12(demultiplexer_13_out12), .out13(demultiplexer_13_out13), .out14(demultiplexer_13_out14),
    .out15(demultiplexer_13_out15), .in(in_88), .sel(undriven_6));
  Demultiplexer #(.select(4), .enable("false")) demultiplexer_14 (
    .out0(demultiplexer_14_out0), .out1(demultiplexer_14_out1), .out2(demultiplexer_14_out2),
    .out3(demultiplexer_14_out3), .out4(demultiplexer_14_out4), .out5(demultiplexer_14_out5),
    .out6(demultiplexer_14_out6), .out7(demultiplexer_14_out7), .out8(demultiplexer_14_out8),
    .out9(demultiplexer_14_out9), .out10(demultiplexer_14_out10), .out11(demultiplexer_14_out11),
    .out12(demultiplexer_14_out12), .out13(demultiplexer_14_out13), .out14(demultiplexer_14_out14),
    .out15(demultiplexer_14_out15), .in(in_68), .sel({{2{undriven_5[3]}}, undriven_5[1:0]}));
  Demultiplexer #(.select(4), .enable("false")) demultiplexer_15 (
    .out0(demultiplexer_14_out0), .out1(demultiplexer_14_out1), .out2(demultiplexer_14_out2),
    .out3(demultiplexer_14_out3), .out4(demultiplexer_14_out4), .out5(demultiplexer_14_out5),
    .out6(demultiplexer_14_out6), .out7(demultiplexer_14_out7), .out8(demultiplexer_14_out8),
    .out9(demultiplexer_14_out9), .out10(demultiplexer_14_out10), .out11(demultiplexer_14_out11),
    .out12(demultiplexer_14_out12), .out13(demultiplexer_14_out13), .out14(demultiplexer_14_out14),
    .out15(demultiplexer_14_out15), .in(in_71), .sel({in_75, IN, in_101, in_100}));
  Demultiplexer #(.select(4), .enable("false")) demultiplexer_16 (
    .out0(demultiplexer_13_out0), .out1(demultiplexer_13_out1), .out2(demultiplexer_13_out2),
    .out3(demultiplexer_13_out3), .out4(demultiplexer_13_out4), .out5(demultiplexer_13_out5),
    .out6(demultiplexer_13_out6), .out7(demultiplexer_13_out7), .out8(demultiplexer_13_out8),
    .out9(demultiplexer_13_out9), .out10(demultiplexer_13_out10), .out11(demultiplexer_13_out11),
    .out12(demultiplexer_13_out12), .out13(demultiplexer_13_out13), .out14(demultiplexer_13_out14),
    .out15(demultiplexer_13_out15), .in(in_89), .sel({in_103, IN, in_101, in_100}));
  not not_5 (not_5_out, in_74);
  and and_9 (and_9_out, in_74, undriven_5[0], undriven_5[1], undriven_5[3], undriven_5[3]);
  and and_10 (and_10_out, not_5_out, undriven_6[0], undriven_6[1], undriven_6[2], undriven_6[3]);
  or or_10 (out_108, and_9_out, and_10_out);

  // Notes on the sheet:
  //   MEMORIA ROM
  //   MODULO ALM
endmodule
