// Logisim project lut.circ as structural Verilog: 1 circuit, main circuit main
module main (
  input  A3,
  input  in_2,
  input  in_3,
  input  in_4,
  input  A2,
  input  in_6,
  input  in_7,
  input  in_8,
  input  in_9,
  input  in_10,
  input  in_11,
  input  in_12,
  input  A1,
  input  in_14,
  input  in_15,
  input  in_16,
  input  in_17,
  input  A0,
  input  in_19,
  input  in_20,
  input  in_21,
  input  in_22,
  input  in_23,
  input  in_24,
  input  in_25,
  input  in_26,
  input  in_27,
  input  in_28,
  input  in_29,
  input  in_30,
  input  in_31,
  input  in_32,
  input  in_33,
  input  in_34,
  input  in_35,
  input  in_36,
  input  in_37,
  input  in_38,
  input  in_39,
  input  in_40,
  input  in_41,
  input  in_42,
  input  in_43,
  input  in_44,
  input  in_45,
  input  in_46,
  input  in_47,
  input  in_48,
  input  in_49,
  input  in_50,
  input  in_51,
  input  in_52,
  input  in_53,
  input  in_54,
  input  in_55,
  input  in_56,
  output out_57,
  output out_58
);

  wire controlled_buffer_1_out, controlled_buffer_2_out, controlled_buffer_3_out, controlled_buffer_4_out,
       controlled_buffer_5_out, controlled_buffer_6_out, controlled_buffer_7_out, controlled_buffer_8_out,
       controlled_buffer_9_out, controlled_buffer_10_out, controlled_buffer_11_out, controlled_buffer_12_out,
       controlled_buffer_13_out, controlled_buffer_14_out, controlled_buffer_15_out,
       controlled_buffer_16_out, controlled_buffer_17_out, controlled_buffer_18_out,
       controlled_buffer_19_out, controlled_buffer_20_out, controlled_buffer_21_out,
       controlled_buffer_22_out, controlled_buffer_23_out, controlled_buffer_24_out,
       controlled_buffer_25_out, controlled_buffer_26_out, controlled_buffer_27_out,
       controlled_buffer_28_out, controlled_buffer_29_out, controlled_buffer_31_out,
       controlled_buffer_32_out, demultiplexer_1_out0, demultiplexer_1_out1, demultiplexer_1_out2,
       demultiplexer_1_out3, demultiplexer_1_out4, demultiplexer_1_out5, demultiplexer_1_out6,
       demultiplexer_1_out7, demultiplexer_1_out8, demultiplexer_1_out9, demultiplexer_1_out10,
       demultiplexer_1_out11, demultiplexer_1_out12, demultiplexer_1_out13, demultiplexer_1_out14,
       demultiplexer_1_out15, demultiplexer_3_out0, demultiplexer_3_out1, demultiplexer_3_out2,
       demultiplexer_3_out3, demultiplexer_3_out4, demultiplexer_3_out5, demultiplexer_3_out6,
       demultiplexer_3_out7, demultiplexer_3_out8, demultiplexer_3_out9, demultiplexer_3_out10,
       demultiplexer_3_out11, demultiplexer_3_out12, demultiplexer_3_out13, demultiplexer_3_out14,
       demultiplexer_3_out15, demultiplexer_4_out0, demultiplexer_4_out1, demultiplexer_4_out2,
       demultiplexer_4_out3, demultiplexer_4_out4, demultiplexer_4_out5, demultiplexer_4_out6,
       demultiplexer_4_out7, demultiplexer_4_out8, demultiplexer_4_out9, demultiplexer_4_out10,
       demultiplexer_4_out11, demultiplexer_4_out12, demultiplexer_4_out13, demultiplexer_4_out14,
       demultiplexer_4_out15;

  Demultiplexer #(.select(4), .enable("false")) demultiplexer_1 (
    .out0(demultiplexer_1_out0), .out1(demultiplexer_1_out1), .out2(demultiplexer_1_out2),
    .out3(demultiplexer_1_out3), .out4(demultiplexer_1_out4), .out5(demultiplexer_1_out5),
    .out6(demultiplexer_1_out6), .out7(demultiplexer_1_out7), .out8(demultiplexer_1_out8),
    .out9(demultiplexer_1_out9), .out10(demultiplexer_1_out10), .out11(demultiplexer_1_out11),
    .out12(demultiplexer_1_out12), .out13(demultiplexer_1_out13), .out14(demultiplexer_1_out14),
    .out15(demultiplexer_1_out15), .in(in_30), .sel({in_49, in_50, in_51, in_52}));
  // AND_Gate _0000 has open pins: in0=A3, in1=A2, in2=A1, in3=A0, out=open
  // AND_Gate _0001 has open pins: in0=A3, in1=A2, in2=A1, in3=A0, out=open
  // AND_Gate _0010 has open pins: in0=A3, in1=A2, in2=A1, in3=A0, out=open
  // AND_Gate _0011 has open pins: in0=A3, in1=A2, in2=A1, in3=A0, out=open
  // AND_Gate _0100 has open pins: in0=A3, in1=A2, in2=A1, in3=A0, out=open
  // AND_Gate _0101 has open pins: in0=A3, in1=A2, in2=A1, in3=A0, out=open
  // AND_Gate _0110 has open pins: in0=A3, in1=A2, in2=A1, in3=A0, out=open
  // AND_Gate _0111 is placed but not wired
  // AND_Gate _0110_2 is placed but not wired
  Demultiplexer #(.select(4), .enable("false")) demultiplexer_2 (
    .out0(demultiplexer_1_out0), .out1(demultiplexer_1_out1), .out2(demultiplexer_1_out2),
    .out3(demultiplexer_1_out3), .out4(demultiplexer_1_out4), .out5(demultiplexer_1_out5),
    .out6(demultiplexer_1_out6), .out7(demultiplexer_1_out7), .out8(demultiplexer_1_out8),
    .out9(demultiplexer_1_out9), .out10(demultiplexer_1_out10), .out11(demultiplexer_1_out11),
    .out12(demultiplexer_1_out12), .out13(demultiplexer_1_out13), .out14(demultiplexer_1_out14),
    .out15(demultiplexer_1_out15), .in(in_35), .sel({in_56, in_55, in_54, in_53}));
  Demultiplexer #(.select(4), .enable("false")) demultiplexer_3 (
    .out0(demultiplexer_3_out0), .out1(demultiplexer_3_out1), .out2(demultiplexer_3_out2),
    .out3(demultiplexer_3_out3), .out4(demultiplexer_3_out4), .out5(demultiplexer_3_out5),
    .out6(demultiplexer_3_out6), .out7(demultiplexer_3_out7), .out8(demultiplexer_3_out8),
    .out9(demultiplexer_3_out9), .out10(demultiplexer_3_out10), .out11(demultiplexer_3_out11),
    .out12(demultiplexer_3_out12), .out13(demultiplexer_3_out13), .out14(demultiplexer_3_out14),
    .out15(demultiplexer_3_out15), .in(in_27), .sel({in_43, in_44, in_45, in_46}));
  Demultiplexer #(.select(4), .enable("false")) demultiplexer_4 (
    .out0(demultiplexer_4_out0), .out1(demultiplexer_4_out1), .out2(demultiplexer_4_out2),
    .out3(demultiplexer_4_out3), .out4(demultiplexer_4_out4), .out5(demultiplexer_4_out5),
    .out6(demultiplexer_4_out6), .out7(demultiplexer_4_out7), .out8(demultiplexer_4_out8),
    .out9(demultiplexer_4_out9), .out10(demultiplexer_4_out10), .out11(demultiplexer_4_out11),
    .out12(demultiplexer_4_out12), .out13(demultiplexer_4_out13), .out14(demultiplexer_4_out14),
    .out15(demultiplexer_4_out15), .in(in_3), .sel({in_20, in_21, in_22, in_23}));
  assign controlled_buffer_1_out = in_26 ? demultiplexer_3_out0 : 1'bz;  // Controlled_Buffer controlled_buffer_1
  assign controlled_buffer_2_out = in_28 ? demultiplexer_3_out1 : 1'bz;  // Controlled_Buffer controlled_buffer_2
  assign controlled_buffer_3_out = in_29 ? demultiplexer_3_out2 : 1'bz;  // Controlled_Buffer controlled_buffer_3
  assign controlled_buffer_4_out = in_31 ? demultiplexer_3_out3 : 1'bz;  // Controlled_Buffer controlled_buffer_4
  assign controlled_buffer_5_out = in_32 ? demultiplexer_3_out4 : 1'bz;  // Controlled_Buffer controlled_buffer_5
  assign controlled_buffer_6_out = in_33 ? demultiplexer_3_out5 : 1'bz;  // Controlled_Buffer controlled_buffer_6
  assign controlled_buffer_7_out = in_36 ? demultiplexer_3_out7 : 1'bz;  // Controlled_Buffer controlled_buffer_7
  assign controlled_buffer_8_out = in_37 ? demultiplexer_3_out8 : 1'bz;  // Controlled_Buffer controlled_buffer_8
  assign controlled_buffer_9_out = in_38 ? demultiplexer_3_out9 : 1'bz;  // Controlled_Buffer controlled_buffer_9
  assign controlled_buffer_10_out = in_39 ? demultiplexer_3_out10 : 1'bz;  // Controlled_Buffer controlled_buffer_10
  assign controlled_buffer_11_out = in_40 ? demultiplexer_3_out11 : 1'bz;  // Controlled_Buffer controlled_buffer_11
  assign controlled_buffer_12_out = in_41 ? demultiplexer_3_out12 : 1'bz;  // Controlled_Buffer controlled_buffer_12
  assign controlled_buffer_13_out = in_42 ? demultiplexer_3_out13 : 1'bz;  // Controlled_Buffer controlled_buffer_13
  assign controlled_buffer_14_out = in_47 ? demultiplexer_3_out14 : 1'bz;  // Controlled_Buffer controlled_buffer_14
  assign controlled_buffer_15_out = in_48 ? demultiplexer_3_out15 : 1'bz;  // Controlled_Buffer controlled_buffer_15
  assign controlled_buffer_16_out = in_2 ? demultiplexer_4_out0 : 1'bz;  // Controlled_Buffer controlled_buffer_16
  assign controlled_buffer_17_out = in_4 ? demultiplexer_4_out1 : 1'bz;  // Controlled_Buffer controlled_buffer_17
  assign controlled_buffer_18_out = in_6 ? demultiplexer_4_out2 : 1'bz;  // Controlled_Buffer controlled_buffer_18
  assign controlled_buffer_19_out = in_7 ? demultiplexer_4_out3 : 1'bz;  // Controlled_Buffer controlled_buffer_19
  assign controlled_buffer_20_out = in_8 ? demultiplexer_4_out4 : 1'bz;  // Controlled_Buffer controlled_buffer_20
  assign controlled_buffer_21_out = in_9 ? demultiplexer_4_out5 : 1'bz;  // Controlled_Buffer controlled_buffer_21
  assign controlled_buffer_22_out = in_11 ? demultiplexer_4_out7 : 1'bz;  // Controlled_Buffer controlled_buffer_22
  assign controlled_buffer_23_out = in_12 ? demultiplexer_4_out8 : 1'bz;  // Controlled_Buffer controlled_buffer_23
  assign controlled_buffer_24_out = in_14 ? demultiplexer_4_out9 : 1'bz;  // Controlled_Buffer controlled_buffer_24
  assign controlled_buffer_25_out = in_15 ? demultiplexer_4_out10 : 1'bz;  // Controlled_Buffer controlled_buffer_25
  assign controlled_buffer_26_out = in_16 ? demultiplexer_4_out11 : 1'bz;  // Controlled_Buffer controlled_buffer_26
  assign controlled_buffer_27_out = in_17 ? demultiplexer_4_out12 : 1'bz;  // Controlled_Buffer controlled_buffer_27
  assign controlled_buffer_28_out = in_19 ? demultiplexer_4_out13 : 1'bz;  // Controlled_Buffer controlled_buffer_28
  assign controlled_buffer_29_out = in_24 ? demultiplexer_4_out14 : 1'bz;  // Controlled_Buffer controlled_buffer_29
  assign demultiplexer_4_out15 = in_25 ? demultiplexer_4_out15 : 1'bz;  // Controlled_Buffer controlled_buffer_30
  assign controlled_buffer_31_out = in_34 ? demultiplexer_3_out6 : 1'bz;  // Controlled_Buffer controlled_buffer_31
  assign controlled_buffer_32_out = in_10 ? demultiplexer_4_out6 : 1'bz;  // Controlled_Buffer controlled_buffer_32
  or or_1 (out_58, controlled_buffer_1_out, controlled_buffer_2_out, controlled_buffer_3_out, controlled_buffer_4_out, controlled_buffer_5_out, controlled_buffer_6_out, controlled_buffer_31_out, controlled_buffer_7_out, controlled_buffer_8_out, controlled_buffer_9_out, controlled_buffer_10_out, controlled_buffer_11_out, controlled_buffer_12_out, controlled_buffer_13_out, controlled_buffer_14_out, controlled_buffer_15_out);
  or or_2 (out_57, controlled_buffer_16_out, controlled_buffer_17_out, controlled_buffer_18_out, controlled_buffer_19_out, controlled_buffer_20_out, controlled_buffer_21_out, controlled_buffer_32_out, controlled_buffer_22_out, controlled_buffer_23_out, controlled_buffer_24_out, controlled_buffer_25_out, controlled_buffer_26_out, controlled_buffer_27_out, controlled_buffer_28_out, controlled_buffer_29_out, demultiplexer_4_out15);
endmodule
