// Logisim project serie-serie.circ as structural Verilog: 1 circuit, main circuit main
module main (
  input  in_1,
  output out_2,
  output out_3
);

  wire clock_1_out, d_ff_1_q, d_ff_2_q, d_ff_3_q, d_ff_4_qn;

  Clock clock_1 (.out(clock_1_out));
  D_Flip_Flop d_ff_1 (.clk(clock_1_out), .D(in_1), .Q(d_ff_1_q));  // open: Qn, preset, en, reset
  D_Flip_Flop d_ff_2 (.clk(clock_1_out), .D(d_ff_1_q), .Q(d_ff_2_q));  // open: Qn, preset, en, reset
  D_Flip_Flop d_ff_3 (.clk(clock_1_out), .D(d_ff_2_q), .Q(d_ff_3_q));  // open: Qn, preset, en, reset
  D_Flip_Flop d_ff_4 (.clk(clock_1_out), .D(d_ff_3_q), .Q(out_2), .Qn(d_ff_4_qn));  // open: preset, en, reset
  not not_1 (out_3, d_ff_4_qn);
endmodule
